// Digital circuit Lab7.dig as structural Verilog
module Lab7 (
  input  clk,
  output [7:0] PC,
  output [7:0] Instr,
  output [7:0] Next_PC,
  output [2:0] Opc,
  output [7:0] Simm,
  output [1:0] R,
  output [1:0] S,
  output [7:0] ValR,
  output [7:0] ValS,
  output [7:0] ValE,
  output BRA,
  output BZ,
  output LD,
  output LDI,
  output ST,
  output ADD,
  output NEG,
  output HLT,
  output [7:0] ValM
);

  wire and_1_out, Reg, Sel_Next_PC, ValR_eq_0;
  wire [0:0] Sel_B;
  wire [1:0] Sel_A;
  wire [7:0] multiplexer_1_out, multiplexer_2_out, multiplexer_3_out, multiplexer_4_out, not_1_out;

  Register #(.Bits(8), .isProgramCounter("true")) u_PC (.D(multiplexer_1_out), .C(clk), .en(1'b1), .Q(PC));
  and and_1 (and_1_out, ValR_eq_0, BZ);
  Multiplexer #(.Bits(8)) multiplexer_1 (.sel(Sel_Next_PC), .in_0(Next_PC), .in_1(ValE), .out(multiplexer_1_out));
  or or_1 (Reg, LD, LDI, ADD, NEG);
  Add #(.Bits(8)) add_1 (.a(PC), .b(8'h1), .c_i(1'b0), .s(Next_PC));  // open: c_o
  ROM #(.AddrBits(8), .Bits(8), .isProgramMemory("true")) rom_1 (.A(PC), .sel(1'b1), .D(Instr));
  or or_2 (Sel_Next_PC, and_1_out, BRA);
  Decoder #(.Selector_Bits(3)) decoder_1 (
    .sel(Instr[7:5]), .out_0(BRA), .out_1(BZ), .out_2(LD), .out_3(LDI), .out_4(ST), .out_5(ADD), .out_6(NEG),
    .out_7(HLT));
  or or_3 (Sel_A[0], ADD, LD, LDI, ST);
  or or_4 (Sel_A[1], NEG, LD, LDI, ST);
  Multiplexer #(.Bits(8)) multiplexer_2 (.sel(LD), .in_0(ValE), .in_1(ValM), .out(multiplexer_2_out));
  RegisterFile #(.Bits(8)) X (
    .Din(multiplexer_2_out), .we(Reg), .Rw(Instr[1:0]), .C(clk), .Ra(Instr[1:0]), .Rb(Instr[3:2]), .Da(ValR),
    .Db(ValS));
  assign not_1_out = ~ValR;  // Not not_1, 8 bits wide
  Comparator #(.Bits(8)) comparator_1 (.a(ValR), .b({8{1'b0}}), .eq(ValR_eq_0));  // open: gt, lt
  or or_5 (Sel_B[0], LD, ST, ADD);
  Multiplexer #(.Selector_Bits(2), .Bits(8)) multiplexer_3 (
    .sel(Sel_A), .in_0(Next_PC), .in_1(ValR), .in_2(not_1_out), .in_3({8{1'b0}}), .out(multiplexer_3_out));
  Multiplexer #(.Selector_Bits(2), .Bits(8)) multiplexer_4 (
    .sel({NEG, Sel_B[0]}), .in_0({{4{Instr[4]}}, Instr[3:0]}), .in_1(ValS), .in_2(8'h1), .in_3({8{1'b0}}),
    .out(multiplexer_4_out));
  Add #(.Bits(8)) add_2 (.a(multiplexer_3_out), .b(multiplexer_4_out), .c_i(1'b0), .s(ValE));  // open: c_o
  RAMDualPort #(.AddrBits(8), .isProgramMemory("true"), .Bits(8)) ramdualport_1 (
    .A(ValE), .Din(ValE), .str(ST), .C(clk), .ld(1'b1), .D(ValM));

  assign Opc = Instr[7:5];
  assign R = Instr[1:0];
  assign S = Instr[3:2];
  assign Simm = {{4{Instr[4]}}, Instr[3:0]};

  // Other names for the same wires on the sheet: Sel_B[1] = NEG

  // Notes on the sheet:
  //   CLK
  //   PC
  //   contents of rom_1 (hex, n*v repeats v):
  //   7f,9*a1,e0
  //   Instr
  //   Next PC
  //   Opc
  //   Eric Mow
  //   Simm
  //   R
  //   S
  //   ValR
  //   ValS
  //   ValR=0
  //   ValE
  //   ValM
endmodule
